// Logisim project m1_33448.circ as structural Verilog
module NOR_T (
  input  x,
  input  y,
  output z
);

  wire transistor_1_out;

  Transistor transistor_1 (.in(1'b1), .out(transistor_1_out), .gate(x));
  Transistor #(.\type ("n")) transistor_2 (.in(1'b0), .out(z), .gate(x));
  Transistor #(.\type ("n")) transistor_3 (.in(1'b0), .out(z), .gate(y));
  Transistor transistor_4 (.in(transistor_1_out), .out(z), .gate(y));
endmodule

module NOT_NOR (
  input  x,
  output y
);

  NOR_T nor_t_1 (.x(x), .y(x), .z(y));
endmodule
